# Fritzing sketch Seniro D  (saved by Fritzing 0.9.10b)

parts:
  Part1 = Arduino Mega 2560 (Rev3)
  L298N1 = L298N motor driver
  M1 = DC Motor [voltage_(max)=6V voltage_(min)=3V]
  M2 = DC Motor [voltage_(max)=6V voltage_(min)=3V]
  Part2 = Arduino Nano (Rev3.0)
  Transceiver1 = nRF24L01
  Transceiver2 = nRF24L01
  Part3 = Thumb Joystick

nets:
  N1: Part1.D9_PWM, L298N1.connector14
  N2: Part1.D8_PWM, L298N1.connector11
  N3: Part1.5V, L298N1.connector7, Transceiver2.connector2
  N4: Part1.GND, L298N1.connector6, Transceiver2.connector1
  N5: Part1.D4_PWM, L298N1.connector12
  N6: Part1.D5_PWM, L298N1.connector16
  N7: Part1.D6_PWM, L298N1.connector15
  N8: Part1.D7_PWM, L298N1.connector13
  N9: Part1.D49, Transceiver2.connector7
  N10: Part1.D50, Transceiver2.connector5
  N11: Part1.D51, Transceiver2.connector3
  N12: Part1.D52, Transceiver2.connector6
  N13: Part1.D53, Transceiver2.connector4
  N14: L298N1.connector0, M2.pin_1
  N15: L298N1.connector1, M2.pin_2
  N16: L298N1.connector2, M1.pin_1
  N17: L298N1.connector4, M1.pin_2
  GND: Part2.GND, Transceiver1.connector1, Part3.GND
  N18: Part2.D2, Transceiver1.connector3
  N19: Part2.D3, Transceiver1.connector5
  N20: Part2.D4, Transceiver1.connector7
  N21: Part2.D5, Transceiver1.connector4
  N22: Part2.D6, Transceiver1.connector6
  5V: Part2.5V, Transceiver1.connector2, Part3.VCC
  N23: Part2.A6, Part3.HORZ
  N24: Part2.A5, Part3.VERT
  N25: Part2.A4, Part3.SEL
